// Logisim project 5-32 decoder.circ as structural Verilog: 1 circuit, main circuit main
module main (
  input  in_1,
  input  in_2,
  input  in_3,
  input  in_4,
  input  in_5,
  input  in_6,
  input  in_7,
  input  in_8,
  input  [2:0] in_9,
  input  in_10,
  input  in_11,
  input  in_12,
  input  in_13,
  input  in_14,
  input  in_15,
  input  in_16,
  input  in_17,
  input  in_18,
  input  in_19,
  input  in_20,
  input  [1:0] in_21,
  input  in_22,
  input  in_23,
  input  in_24,
  input  in_25,
  input  in_26,
  input  in_27,
  input  in_28,
  input  in_29,
  input  in_30,
  input  in_31,
  input  in_32,
  input  in_33,
  input  in_34
);

  wire decoder_1_out0, decoder_1_out1, decoder_1_out2, decoder_1_out3;

  Decoder #(.select(2)) decoder_1 (
    .out0(decoder_1_out0), .out1(decoder_1_out1), .out2(decoder_1_out2), .out3(decoder_1_out3), .sel(in_21));  // open: en
  Decoder #(.select(3)) decoder_2 (
    .out0(in_1), .out1(in_2), .out2(in_3), .out3(in_4), .out4(in_5), .out5(in_6), .out6(in_7), .out7(in_8),
    .sel(in_9), .en(decoder_1_out0));
  Decoder #(.select(3)) decoder_3 (
    .out0(in_10), .out1(in_11), .out2(in_12), .out3(in_13), .out4(in_14), .out5(in_15), .out6(in_16),
    .out7(in_17), .sel(in_9), .en(decoder_1_out1));
  Decoder #(.select(3)) decoder_4 (
    .out0(in_18), .out1(in_19), .out2(in_20), .out3(in_22), .out4(in_23), .out5(in_24), .out6(in_25),
    .out7(in_26), .sel(in_9), .en(decoder_1_out2));
  Decoder #(.select(3)) decoder_5 (
    .out0(in_27), .out1(in_28), .out2(in_29), .out3(in_30), .out4(in_31), .out5(in_32), .out6(in_33),
    .out7(in_34), .sel(in_9), .en(decoder_1_out3));
endmodule
