// Logisim project mod4down.circ as structural Verilog: 1 circuit, main circuit main
module main (
  input  [1:0] in_1
);

  wire clock_1_out;
  wire [1:0] counter_1_q, rom_1_data;

  ROM #(.addrWidth(2), .dataWidth(2)) rom_1 (.addr(counter_1_q), .data(rom_1_data));  // open: sel
  Clock clock_1 (.out(clock_1_out));
  Counter #(.width(2), .max('h3)) counter_1 (
    .D(rom_1_data), .Q(counter_1_q), .clk(clock_1_out));  // open: load, count, carry, clr

  // Notes on the sheet:
  //   contents of rom_1 (hex, n*v repeats v):
  //   1 2 3
endmodule
